// Logisim project Team3 기본컴퓨터설계 - 완성.circ as structural Verilog
module main (
  input  _0_INC_1_DEC,
  output [2:0] Select,
  output [2:0] IR,
  output [4:0] out_4,
  output [7:0] AC,
  output [7:0] AR,
  output [7:0] DR,
  output [2:0] out_8,
  output [7:0] out_9
);

  wire clock_1_out, Control_circuit_out_12, Control_circuit_out_13, Control_circuit_out_14,
       Control_circuit_out_15, Control_circuit_out_16, Control_circuit_out_17, Control_circuit_out_18,
       Control_circuit_out_19, decoder_1_out0, decoder_1_out1, decoder_1_out2, decoder_1_out3,
       decoder_1_out4, decoder_2_out0, decoder_2_out1, decoder_2_out2, decoder_2_out3, decoder_2_out4,
       Flag_out, INC_out, LOAD_2_out, LOAD_3_out, LOAD_4_out, LOAD_5_out, LOAD_out, not_1_out, or_1_out,
       READ_out, Write_out, \산술_논리회로_out_6 ;
  wire [2:0] counter_1_q;
  wire [3:0] \PC_레지스터_out_5 , \PC_레지스터_out_5_2 ;
  wire [4:0] \AR_레지스터_out_4 ;
  wire [7:0] ram_1_data, \산술_논리회로_out_5 ;

  Clock clock_1 (.out(clock_1_out));
  Counter #(.width(3), .max('h7)) counter_1 (
    .load(or_1_out), .D(3'b000), .count(not_1_out), .Q(counter_1_q), .clk(clock_1_out));  // open: carry, clr
  not not_1 (not_1_out, or_1_out);
  or or_1 (or_1_out, Control_circuit_out_12, Control_circuit_out_15, Control_circuit_out_17, Control_circuit_out_18, Control_circuit_out_19);
  and Flag (Flag_out, _0_INC_1_DEC, decoder_1_out1);
  Decoder #(.select(3)) decoder_1 (
    .out0(decoder_1_out0), .out1(decoder_1_out1), .out2(decoder_1_out2), .out3(decoder_1_out3),
    .out4(decoder_1_out4), .sel(counter_1_q));  // open: out5, out6, out7, en
  Decoder #(.select(3)) decoder_2 (
    .out0(decoder_2_out0), .out1(decoder_2_out1), .out2(decoder_2_out2), .out3(decoder_2_out3),
    .out4(decoder_2_out4), .sel(out_8));  // open: out5, out6, out7, en
  \산술_논리_회로  \u_산술_논리회로  (
    .AC(DR), .DC(AC), .out_6(\산술_논리회로_out_6 ), .And(Control_circuit_out_12), .Add(Control_circuit_out_15),
    .out_5(\산술_논리회로_out_5 ));
  Register #(.width(1)) \E_레지스터  (.D(\산술_논리회로_out_6 ), .en(Control_circuit_out_15), .clk(clock_1_out));  // open: Q, clr
  control_logic_circuit Control_circuit (
    .T0(decoder_1_out0), .T1(decoder_1_out1), .T2(decoder_1_out2), .T3(decoder_1_out3), .T4(decoder_1_out4),
    .out_11(Select), .D1(decoder_2_out1), .D2(decoder_2_out2), .D3(decoder_2_out3), .D4(decoder_2_out4),
    .D0(decoder_2_out0), .out_12(Control_circuit_out_12), .out_13(Control_circuit_out_13),
    .out_15(Control_circuit_out_15), .out_14(Control_circuit_out_14), .out_16(Control_circuit_out_16),
    .out_18(Control_circuit_out_18), .out_19(Control_circuit_out_19), .out_17(Control_circuit_out_17));
  or READ (READ_out, Control_circuit_out_13, decoder_1_out1, Control_circuit_out_14, Control_circuit_out_16);
  buf Write (Write_out, Control_circuit_out_18);  // OR_Gate
  or LOAD (LOAD_out, decoder_1_out0, decoder_1_out2);
  buf INC (INC_out, decoder_1_out1);  // OR_Gate
  or LOAD_2 (LOAD_2_out, Control_circuit_out_13, Control_circuit_out_14, Control_circuit_out_16);
  or LOAD_3 (LOAD_3_out, Control_circuit_out_12, Control_circuit_out_15, Control_circuit_out_17);
  buf LOAD_4 (LOAD_4_out, decoder_1_out1);  // OR_Gate
  or LOAD_5 (LOAD_5_out, Control_circuit_out_19, Flag_out);
  \AR_레지스터  \AR_레지스터  (.out_5(AR), .in_1(out_9), .in_3(clock_1_out), .in_2(LOAD_out), .out_4(\AR_레지스터_out_4 ));
  \PC_레지스터  \PC_레지스터  (
    .in_2(INC_out), .in_1(out_9), .in_4(clock_1_out), .in_3(LOAD_5_out),
    .out_5({\PC_레지스터_out_5_2 , \PC_레지스터_out_5 }));
  \DR_레지스터  \DR_레지스터  (.in_2(out_9), .out_5(DR), .in_4(clock_1_out), .in_3(LOAD_2_out));  // open: in_1
  \DR_레지스터  \AC_레지스터  (.in_2(\산술_논리회로_out_5 ), .out_5(AC), .in_4(clock_1_out), .in_3(LOAD_3_out));  // open: in_1
  \IR_레지스터  \IR_레지스터  (.in_1(out_9), .out_4({IR, out_4}), .in_3(clock_1_out), .in_2(LOAD_4_out));
  Hex_Digit_Display hex_digit_display_1 (.value(\PC_레지스터_out_5_2 ));  // open: dp
  RAM #(.addrWidth(5), .bus("separate")) ram_1 (
    .addr(\AR_레지스터_out_4 ), .din(out_9), .data(ram_1_data), .str(Write_out), .clk(clock_1_out), .ld(READ_out));  // open: sel, clr
  Hex_Digit_Display hex_digit_display_2 (.value(\PC_레지스터_out_5 ));  // open: dp
  \bus_시스템  \bus_시스템_1  (
    .Select(Select), .IR({IR, out_4}), .MEMORY(ram_1_data), .AC(AC), .AR(AR), .DR(DR), .out_9(out_9),
    .PC({\PC_레지스터_out_5_2 , \PC_레지스터_out_5 }), .out_8(out_8));

  // Notes on the sheet:
  //   SC
  //   T0 ~ T4
  //   D0~ D4
  //   Memory Unit
  //   PC
endmodule

module \AR_레지스터  (
  input  [7:0] in_1,
  input  in_2,
  input  in_3,
  output [4:0] out_4,
  output [7:0] out_5
);

  Register #(.width(5)) register_1 (.D(in_1[4:0]), .en(in_2), .Q(out_4), .clk(in_3));  // open: clr

  assign out_5 = {3'b000, out_4};
endmodule

module \PC_레지스터  (
  input  [7:0] in_1,
  input  in_2,
  input  in_3,
  input  in_4,
  output [7:0] out_5
);

  wire or_1_out;
  wire [4:0] adder_1_out, adder_2_out, adder_3_out, multiplexer_1_out, not_1_out;

  or or_1 (or_1_out, in_2, in_3);
  Register #(.width(5)) register_1 (.D(multiplexer_1_out), .en(or_1_out), .Q(out_5[4:0]), .clk(in_4));  // open: clr
  Multiplexer #(.select(2), .width(5)) multiplexer_1 (
    .in0(out_5[4:0]), .in1(in_1[4:0]), .in2(adder_1_out), .in3(adder_3_out), .out(multiplexer_1_out),
    .sel({in_2, in_3}));  // open: en
  Adder #(.width(5)) adder_1 (.a(out_5[4:0]), .b({5{1'b0}}), .out(adder_1_out), .cin(in_2));  // open: cout
  assign not_1_out = ~out_5[4:0];  // NOT_Gate not_1, 5 bits wide
  Adder #(.width(5)) adder_2 (.a(out_5[4:0]), .b(not_1_out), .out(adder_2_out));  // open: cin, cout
  Adder #(.width(5)) adder_3 (.a(out_5[4:0]), .b(adder_2_out), .out(adder_3_out));  // open: cin, cout

  assign out_5[7:5] = 3'b000;
endmodule

module \DR_레지스터  (
  input  in_1,
  input  [7:0] in_2,
  input  in_3,
  input  in_4,
  output [7:0] out_5
);

  wire [7:0] register_1_q;

  Register register_1 (.D(in_2), .en(in_3), .Q(register_1_q), .clk(in_4));  // open: clr
  Adder adder_1 (.a(register_1_q), .b({8{1'b0}}), .out(out_5), .cin(in_1));  // open: cout
endmodule

// 통합 버스 시스템
module \bus_시스템  (
  input  [2:0] Select,
  input  [7:0] IR,
  input  [7:0] AC,
  input  [7:0] DR,
  input  [7:0] PC,
  input  [7:0] AR,
  input  [7:0] MEMORY,
  output [2:0] out_8,
  output [7:0] out_9
);

  wire decoder_1_out1, decoder_1_out2, decoder_1_out3, decoder_1_out4, decoder_1_out5, decoder_1_out7;

  Decoder #(.select(3)) decoder_1 (
    .out1(decoder_1_out1), .out2(decoder_1_out2), .out3(decoder_1_out3), .out4(decoder_1_out4),
    .out5(decoder_1_out5), .out7(decoder_1_out7), .sel(Select));  // open: out0, out6, en
  assign out_9 = decoder_1_out5 ? IR : 8'bz;  // Controlled_Buffer controlled_buffer_1
  assign out_9 = decoder_1_out4 ? AC : 8'bz;  // Controlled_Buffer controlled_buffer_2
  assign out_9 = decoder_1_out3 ? DR : 8'bz;  // Controlled_Buffer controlled_buffer_3
  assign out_9 = decoder_1_out2 ? PC : 8'bz;  // Controlled_Buffer controlled_buffer_4
  assign out_9 = decoder_1_out1 ? AR : 8'bz;  // Controlled_Buffer controlled_buffer_5
  assign out_9 = decoder_1_out7 ? MEMORY : 8'bz;  // Controlled_Buffer controlled_buffer_6

  assign out_8 = IR[7:5];
endmodule

module \IR_레지스터  (
  input  [7:0] in_1,
  input  in_2,
  input  in_3,
  output [7:0] out_4
);

  Register register_1 (.D(in_1), .en(in_2), .Q(out_4), .clk(in_3));  // open: clr
endmodule

module \산술_논리_회로  (
  input  And,
  input  Add,
  input  [7:0] AC,
  input  [7:0] DC,
  output [7:0] out_5,
  output out_6
);

  wire [7:0] adder_1_out, and_1_out;

  assign and_1_out = AC & DC;  // AND_Gate and_1, 8 bits wide
  Adder adder_1 (.a(AC), .b(DC), .out(adder_1_out), .cout(out_6));  // open: cin
  Multiplexer #(.select(2), .width(8)) multiplexer_1 (
    .in0(AC), .in1(and_1_out), .in2(adder_1_out), .out(out_5), .sel({Add, And}));  // open: in3, en
endmodule

module control_logic_circuit (
  input  T0,
  input  T1,
  input  T2,
  input  T3,
  input  T4,
  input  D0,
  input  D1,
  input  D2,
  input  D3,
  input  D4,
  output [2:0] out_11,
  output out_12,
  output out_13,
  output out_14,
  output out_15,
  output out_16,
  output out_17,
  output out_18,
  output out_19
);

  and D0T4 (out_12, D0, T4);
  and D0T3 (out_13, T3, D0);
  and D1T3 (out_14, T3, D1);
  and D1T4 (out_15, T4, D1);
  and D2T3 (out_16, T3, D2);
  and D2T4 (out_17, T4, D2);
  and D3T3 (out_18, T3, D3);
  and D4T3 (out_19, T3, D4);
  or S0 (out_11[0], T1, T2, out_13, out_14, out_19, out_16, out_17);
  or S1 (out_11[1], T1, T0, out_13, out_14, out_16, out_17);
  or S2 (out_11[2], T1, T2, out_13, out_14, out_16, out_18);
endmodule
