// Logisim project A-1.circ as structural Verilog: 1 circuit, main circuit main
module main (
  input  D,
  input  D_2,
  output Q,
  output Q_2
);

  wire clock_1_out, Master_q, not_1_out;

  Clock clock_1 (.out(clock_1_out));
  D_Flip_Flop Master (.clk(clock_1_out), .D(D), .Q(Master_q));  // open: Qn, preset, en, reset
  not not_1 (not_1_out, clock_1_out);
  buf Master_2 (Q_2, D_2);
  D_Flip_Flop Slave (.clk(not_1_out), .D(Master_q), .Q(Q));  // open: Qn, preset, en, reset
endmodule
