// Logisim project B-5.circ as structural Verilog: 1 circuit, main circuit main
module main (
  input  x,
  output y
);

  wire A_q, and_1_out, and_2_out, and_3_out, and_4_out, and_5_out, and_6_out, B_q, C_q, clock_1_out,
       not_1_out, not_2_out, not_3_out, not_4_out, not_5_out, not_6_out, or_1_out, or_2_out;

  not not_1 (not_1_out, x);
  not not_2 (not_2_out, x);
  and and_1 (and_1_out, B_q, C_q, x);
  not not_3 (not_3_out, A_q);
  and and_2 (and_2_out, not_4_out, not_2_out);
  not not_4 (not_4_out, C_q);
  not not_5 (not_5_out, B_q);
  and and_3 (and_3_out, A_q, x);
  and and_4 (and_4_out, C_q, not_1_out);
  and and_5 (and_5_out, not_3_out, not_5_out, not_1_out);
  and and_6 (and_6_out, not_3_out, not_5_out, x);
  or or_1 (or_1_out, A_q, and_2_out, and_1_out);
  or or_2 (or_2_out, and_3_out, and_4_out, and_5_out);
  Clock clock_1 (.out(clock_1_out));
  D_Flip_Flop A (.clk(clock_1_out), .D(and_6_out), .Q(A_q));  // open: Qn, preset, en, reset
  D_Flip_Flop B (.clk(clock_1_out), .D(or_1_out), .Q(B_q));  // open: Qn, preset, en, reset
  D_Flip_Flop C (.clk(clock_1_out), .D(or_2_out), .Q(C_q));  // open: Qn, preset, en, reset
  not not_6 (not_6_out, A_q);
  and and_7 (y, not_6_out, x);
endmodule
